// Logisim project main.circ as structural Verilog: 11 circuits, main circuit main
module main (
  input  [31:0] enter_here,
  output [31:0] out_2,
  output [31:0] out_3,
  output [31:0] out_4
);

  wire ADD_out, and_1_out, bcd_to_7_segment_decoder_3_p1, binary_to_bcd_converter_1_p2,
       binary_to_bcd_converter_1_p4, Burger_out, CLK, CokeFloat_out, CONFIRM_out, controlled_buffer_3_out,
       Done, Done_out, foods_1_inputdone, foods_1_out_7, foods_1_out_8, foods_1_out_9, HALT, InEn, MINUS_out,
       money_1_out_3, NO_out, not_1_out, or_1_out, OutEn1, OutEn2, quantity_1_done, RST, RSTT, Spaghetti_out,
       Stage_1, Stage_2, Stage_3, Stage_4;
  wire [0:0] YES_out;
  wire [3:3] cpu_1_mainsignals;
  wire [7:0] controlled_buffer_5_out, cpu_1_adrbus, quantity_1_amount;
  wire [31:0] cpu_1_dataout, Data, foods_1_stage_1_output, Item, multiplexer_1_out, quantity_1_floatamount;

  Clock clock_1 (.out(CLK));
  Multiplexer #(.width(32)) multiplexer_1 (.in0(Data), .in1(Item), .out(multiplexer_1_out), .sel(InEn));
  InputStage inputstage_1 (.InputIns(Data), .INP(InEn), .CLK(CLK), .InputStages({Stage_4, Stage_3, Stage_2, Stage_1}));
  not not_1 (not_1_out, cpu_1_mainsignals[3]);
  CPU cpu_1 (
    .CLK(CLK), .RST(RST), .DataIn(multiplexer_1_out), .InputDone(Done), .DataOut(cpu_1_dataout),
    .MainSignals({HALT, cpu_1_mainsignals[3], OutEn1, InEn, OutEn2}), .AdrBus(cpu_1_adrbus));
  RAM #(.dataWidth(32)) ram_1 (
    .addr(cpu_1_adrbus), .we(cpu_1_mainsignals[3]), .oe(not_1_out), .clk(CLK), .din(cpu_1_dataout),
    .dout(Data));
  Button button_1 (.out(RST));
  Button u_Done (.out(Done_out));
  QUANTITY quantity_1 (
    .CLK(CLK), .RST(RSTT), .inc(ADD_out), .dec(MINUS_out), .AMOUNT(quantity_1_amount),
    .FloatAmount(quantity_1_floatamount), .Done(quantity_1_done));
  Button ADD (.out(ADD_out));
  Money money_1 (.enter_here(enter_here), .total_charges(out_3), .out_3(money_1_out_3));
  Button CONFIRM (.out(CONFIRM_out));
  LED led_1 (.in(foods_1_out_7));
  LED led_2 (.in(Stage_1));
  LED led_3 (.in(Stage_2));
  and and_1 (and_1_out, Done_out, quantity_1_done);
  assign Done = Stage_2 ? and_1_out : 1'bz;  // Controlled_Buffer controlled_buffer_1
  Button MINUS (.out(MINUS_out));
  LED led_4 (.in(Stage_4));
  assign Item = Stage_4 ? enter_here : 32'bz;  // Controlled_Buffer controlled_buffer_2
  assign controlled_buffer_3_out = money_1_out_3 ? CONFIRM_out : 1'bz;  // Controlled_Buffer controlled_buffer_3
  assign Done = Stage_4 ? controlled_buffer_3_out : 1'bz;  // Controlled_Buffer controlled_buffer_4
  Button Burger (.out(Burger_out));
  _7_Segment_Display u_7_segment_display_1 ();  // open: g, f, a, b, e, d, c, dp
  // BCD_to_7_Segment_decoder bcd_to_7_segment_decoder_1: pin names not known
  assign controlled_buffer_5_out = Stage_2 ? quantity_1_amount : 8'bz;  // Controlled_Buffer controlled_buffer_5
  // Binary_to_BCD_converter #(.binvalue(8)) binary_to_bcd_converter_1: pin names not known; wires that end beside it: controlled_buffer_5_out, binary_to_bcd_converter_1_p2, binary_to_bcd_converter_1_p2, binary_to_bcd_converter_1_p4
  FOODS foods_1 (
    .WE(Stage_1), .CLK(CLK), .in_4(Burger_out), .in_5(Spaghetti_out), .in_6(CokeFloat_out), .RST(RSTT),
    .InputDone(foods_1_inputdone), .out_7(foods_1_out_7), .out_8(foods_1_out_8), .out_9(foods_1_out_9),
    .Stage_1_Output(foods_1_stage_1_output));
  Button Spaghetti (.out(Spaghetti_out));
  Button CokeFloat (.out(CokeFloat_out));
  _7_Segment_Display u_7_segment_display_2 ();  // open: g, f, a, b, e, d, c, dp
  // BCD_to_7_Segment_decoder bcd_to_7_segment_decoder_2: pin names not known; wires that end beside it: binary_to_bcd_converter_1_p4
  assign Item = Stage_2 ? quantity_1_floatamount : 32'bz;  // Controlled_Buffer controlled_buffer_6
  LED led_5 (.in(foods_1_out_8));
  _7_Segment_Display u_7_segment_display_3 ();  // open: g, f, a, b, e, d, c, dp
  // BCD_to_7_Segment_decoder bcd_to_7_segment_decoder_3: pin names not known; wires that end beside it: bcd_to_7_segment_decoder_3_p1, bcd_to_7_segment_decoder_3_p1
  assign Item = Stage_1 ? foods_1_stage_1_output : 32'bz;  // Controlled_Buffer controlled_buffer_7
  assign Done = Stage_1 ? foods_1_inputdone : 1'bz;  // Controlled_Buffer controlled_buffer_8
  Register #(.width(32)) register_1 (.D(Data), .en(OutEn1), .clk(CLK), .Q(out_3), .clr(RST));
  Register #(.width(32)) register_2 (.D(Data), .en(OutEn2), .clk(CLK), .Q(out_4), .clr(RST));
  Button YES (.out(YES_out[0]));
  Button NO (.out(NO_out));
  LED led_6 (.in(foods_1_out_9));
  LED led_7 (.in(Stage_3));
  assign RSTT = Stage_3 ? YES_out[0] : 1'bz;  // Controlled_Buffer controlled_buffer_9
  or or_1 (or_1_out, YES_out[0], NO_out);
  assign Done = Stage_3 ? or_1_out : 1'bz;  // Controlled_Buffer controlled_buffer_10
  assign Item = Stage_3 ? {{31{1'b0}}, YES_out[0]} : 32'bz;  // Controlled_Buffer controlled_buffer_11
  LED led_8 (.in(HALT));

  assign out_2 = enter_here;

  // Other names for the same wires on the sheet: payment[31:0] = Item; quant[31:0] = Item; res[31:0] = Item

  // Notes on the sheet:
  //   RESTART
  //   SELECT FOOD:
  //   ENTER QUANTITY:
  //   ENTER PAYMENT:
  //   BURGER - 50.50 PESOS
  //   SPAGHETTI - 60.20 PESOS
  //   ADD MORE? YES/NO
  //   CokeFloat - 40.80 PESOS
  //   TOTAL PAYMENT
  //   TOTAL CHARGES
  //   TOTAL CHANGE
  //   TRANSACTION DONE!!
endmodule

module CPU (
  input  CLK,
  input  RST,
  input  [31:0] DataIn,
  input  InputDone,
  output [31:0] DataOut,
  output [4:0] MainSignals,
  output [7:0] AdrBus
);

  wire AdrSelect, AluEn, decoder_1_out0, decoder_1_out1, IsOne, JumpEq, LoadIn, multiplexer_1_out,
       multiplexer_2_out, not_1_out, RegSelect, RegWrite, UpdatePc;
  wire [1:0] OutEn;
  wire [7:0] adder_1_out, multiplexer_4_out, PC_q;
  wire [31:0] AluOut, IR_q, multiplexer_3_out, RegATunnel, RegB_q;

  Decoder decoder_1 (.out0(decoder_1_out0), .out1(decoder_1_out1), .sel(RegSelect), .en(RegWrite));
  Comparator #(.width(32)) comparator_1 (.a(RegATunnel), .b(32'h1), .eq(IsOne));  // open: gt, lt
  Multiplexer multiplexer_1 (.in0(UpdatePc), .in1(IsOne), .out(multiplexer_1_out), .sel(JumpEq));
  Multiplexer multiplexer_2 (.in0(multiplexer_1_out), .in1(1'b0), .out(multiplexer_2_out), .sel(MainSignals[4]));
  Multiplexer #(.width(32)) multiplexer_3 (.in0(DataIn), .in1(AluOut), .out(multiplexer_3_out), .sel(AluEn));
  Register #(.width(32)) RegA (.D(multiplexer_3_out), .en(decoder_1_out0), .clk(CLK), .Q(RegATunnel), .clr(RST));
  Register #(.width(32)) RegB (.D(DataIn), .en(decoder_1_out1), .clk(CLK), .Q(RegB_q), .clr(RST));
  Register #(.width(32)) IR (.D(DataIn), .en(LoadIn), .clk(CLK), .Q(IR_q), .clr(RST));
  Multiplexer #(.width(8)) multiplexer_4 (.in0(adder_1_out), .in1(IR_q[7:0]), .out(multiplexer_4_out), .sel(JumpEq));
  Register PC (.D(multiplexer_4_out), .en(multiplexer_2_out), .clk(CLK), .Q(PC_q), .clr(RST));
  Adder adder_1 (.a(8'h1), .b(PC_q), .out(adder_1_out));  // open: cin, cout
  Multiplexer #(.width(32)) multiplexer_5 (.in0(RegATunnel), .in1(RegB_q), .out(DataOut), .sel(RegSelect));
  ALU alu_1 (.A(RegATunnel), .B(RegB_q), .AluEn(AluEn), .AluIns(IR_q[31:28]), .AluOut(AluOut));
  ControlUnit controlunit_1 (
    .InputDone(InputDone), .Instruction(IR_q[31:28]), .CLK(CLK), .RST(RST), .RegWrite(RegWrite),
    .RegSelect(RegSelect), .AdrSelect(AdrSelect), .LoadIn(LoadIn), .UpdatePC(UpdatePc), .JumpEq(JumpEq),
    .InEn(MainSignals[1]), .OutEn(OutEn), .MemWrite(MainSignals[3]), .Halt(MainSignals[4]), .AluEn(AluEn));
  not not_1 (not_1_out, AdrSelect);
  Multiplexer #(.width(8)) multiplexer_6 (.in0(IR_q[7:0]), .in1(PC_q), .out(AdrBus), .sel(not_1_out));
  OutputUnit outputunit_1 (.OutputInst(OutEn), .Out2(MainSignals[0]), .Out1(MainSignals[2]));

  // Other names for the same wires on the sheet: InEn = MainSignals[1]; MemWrite = MainSignals[3];
  //   Halt = MainSignals[4]
endmodule

module ControlUnit (
  input  InputDone,
  input  [3:0] Instruction,
  input  CLK,
  input  RST,
  output RegWrite,
  output RegSelect,
  output AdrSelect,
  output LoadIn,
  output UpdatePC,
  output JumpEq,
  output InEn,
  output [1:0] OutEn,
  output MemWrite,
  output Halt,
  output AluEn
);

  wire [4:0] nextstatelogic_1_nextstate, StateRegister_q;

  NextStateLogic nextstatelogic_1 (
    .Input(InputDone), .Instruction(Instruction), .CurrentState(StateRegister_q),
    .NextState(nextstatelogic_1_nextstate));
  Register #(.width(5)) StateRegister (
    .D(nextstatelogic_1_nextstate), .en(1'b1), .clk(CLK), .Q(StateRegister_q), .clr(RST));
  OutputLogic outputlogic_1 (
    .CurrentState(StateRegister_q), .RegWrite(RegWrite), .RegSelect(RegSelect), .AdrSelect(AdrSelect),
    .LoadIn(LoadIn), .UpdatePC(UpdatePC), .JumpEq(JumpEq), .InEn(InEn), .OutEn(OutEn), .MemWrite(MemWrite),
    .Halt(Halt), .AluEn(AluEn));
endmodule

module OutputLogic (
  input  [4:0] CurrentState,
  output RegWrite,
  output RegSelect,
  output AdrSelect,
  output LoadIn,
  output UpdatePC,
  output JumpEq,
  output InEn,
  output [1:0] OutEn,
  output MemWrite,
  output Halt,
  output AluEn
);

  wire and_1_out, and_2_out, and_3_out, and_5_out, and_6_out, and_7_out, and_8_out, and_17_out, and_18_out,
       not_1_out, not_2_out, not_3_out, not_4_out, not_5_out;

  not not_1 (not_1_out, CurrentState[4]);
  not not_2 (not_2_out, CurrentState[3]);
  not not_3 (not_3_out, CurrentState[2]);
  not not_4 (not_4_out, CurrentState[1]);
  not not_5 (not_5_out, CurrentState[0]);
  and and_1 (and_1_out, CurrentState[4], not_2_out, not_3_out, CurrentState[1]);
  and and_2 (and_2_out, CurrentState[4], not_2_out, not_4_out, not_5_out);
  and and_3 (and_3_out, CurrentState[4], not_3_out, not_4_out, not_5_out);
  and and_4 (RegSelect, CurrentState[4], not_2_out, not_3_out, not_4_out, not_5_out);
  and and_5 (and_5_out, CurrentState[4], not_2_out, not_3_out, not_4_out);
  and and_6 (and_6_out, not_1_out, not_2_out, not_3_out, CurrentState[1], not_5_out);
  and and_7 (and_7_out, CurrentState[4], not_2_out, not_4_out, CurrentState[0]);
  and and_8 (and_8_out, CurrentState[4], not_3_out, not_4_out, CurrentState[0]);
  and and_9 (LoadIn, not_1_out, not_2_out, not_3_out, not_4_out, CurrentState[0]);
  and and_10 (UpdatePC, not_1_out, not_2_out, not_3_out, not_4_out, CurrentState[0]);
  and and_11 (JumpEq, CurrentState[4], not_2_out, CurrentState[2], CurrentState[1], CurrentState[0]);
  and and_12 (InEn, CurrentState[4], not_2_out, CurrentState[2], not_4_out, not_5_out);
  and and_13 (OutEn[1], CurrentState[4], CurrentState[3], not_3_out, not_4_out, CurrentState[0]);
  and and_14 (OutEn[0], CurrentState[4], not_2_out, CurrentState[2], not_4_out, CurrentState[0]);
  and and_15 (MemWrite, CurrentState[4], not_2_out, not_3_out, not_4_out, CurrentState[0]);
  and and_16 (Halt, CurrentState[4], not_2_out, CurrentState[2], CurrentState[1], not_5_out);
  and and_17 (and_17_out, CurrentState[4], not_2_out, not_3_out, CurrentState[1]);
  and and_18 (and_18_out, CurrentState[4], CurrentState[3], not_3_out, not_4_out, not_5_out);
  or or_1 (RegWrite, and_1_out, and_2_out, and_3_out);
  or or_2 (AdrSelect, and_5_out, and_6_out, and_7_out, and_8_out);
  or or_3 (AluEn, and_17_out, and_18_out);
endmodule

module NextStateLogic (
  input  Input,
  input  [3:0] Instruction,
  input  [4:0] CurrentState,
  output [4:0] NextState
);

  wire and_1_out, and_2_out, and_3_out, and_4_out, and_6_out, and_7_out, and_8_out, and_9_out, and_10_out,
       and_11_out, and_12_out, and_13_out, and_14_out, not_1_out, not_2_out, not_3_out, not_4_out, not_5_out,
       not_6_out, not_7_out, not_8_out, not_9_out;

  not not_1 (not_1_out, Input);
  not not_2 (not_2_out, Instruction[3]);
  not not_3 (not_3_out, Instruction[2]);
  not not_4 (not_4_out, Instruction[1]);
  not not_5 (not_5_out, CurrentState[4]);
  not not_6 (not_6_out, CurrentState[3]);
  not not_7 (not_7_out, CurrentState[2]);
  not not_8 (not_8_out, CurrentState[1]);
  not not_9 (not_9_out, CurrentState[0]);
  and and_1 (and_1_out, not_2_out, not_5_out, not_6_out, not_7_out, CurrentState[1], not_9_out);
  and and_2 (and_2_out, not_3_out, not_4_out, not_5_out, not_6_out, not_7_out, CurrentState[1], not_9_out);
  and and_3 (and_3_out, not_1_out, CurrentState[4], not_6_out, CurrentState[2], not_9_out);
  and and_4 (and_4_out, CurrentState[4], not_6_out, CurrentState[2], CurrentState[1], not_9_out);
  and and_5 (NextState[3], Instruction[3], not_3_out, not_4_out, not_5_out, not_6_out, not_7_out, CurrentState[1], not_9_out);
  and and_6 (and_6_out, not_2_out, Instruction[2], not_5_out, not_6_out, not_7_out, CurrentState[1], not_9_out);
  and and_7 (and_7_out, not_1_out, CurrentState[4], not_6_out, CurrentState[2], not_9_out);
  and and_8 (and_8_out, CurrentState[4], not_6_out, CurrentState[2], CurrentState[1], not_9_out);
  and and_9 (and_9_out, not_5_out, not_6_out, not_7_out, not_8_out, CurrentState[0]);
  and and_10 (and_10_out, CurrentState[4], not_6_out, CurrentState[2], CurrentState[1], not_9_out);
  and and_11 (and_11_out, not_2_out, Instruction[1], not_5_out, not_6_out, not_7_out, CurrentState[1], not_9_out);
  and and_12 (and_12_out, not_5_out, not_6_out, not_7_out, not_8_out, not_9_out);
  and and_13 (and_13_out, not_2_out, Instruction[0], not_5_out, not_6_out, not_7_out, not_9_out);
  and and_14 (and_14_out, not_3_out, not_4_out, Instruction[0], not_5_out, not_6_out, not_7_out, not_9_out);
  or or_1 (NextState[4], and_1_out, and_2_out, and_3_out, and_4_out);
  or or_2 (NextState[2], and_6_out, and_7_out, and_8_out);
  or or_3 (NextState[1], and_9_out, and_10_out, and_11_out);
  or or_4 (NextState[0], and_12_out, and_13_out, and_14_out);
endmodule

module ALU (
  input  [31:0] A,
  input  [31:0] B,
  input  AluEn,
  input  [3:0] AluIns,
  output [31:0] AluOut
);

  wire comparator_1_eq, comparator_1_gt, comparator_1_lt;
  wire [31:0] controlled_buffer_1_out, fpadder_1_out, fpmultiplier_1_out, fpsubtractor_1_out;

  FPAdder fpadder_1 (.a(A), .b(B), .out(fpadder_1_out));
  FPMultiplier fpmultiplier_1 (.a(A), .b(B), .out(fpmultiplier_1_out));
  FPSubtractor fpsubtractor_1 (.a(A), .b(B), .out(fpsubtractor_1_out));
  Comparator #(.mode("unsigned"), .width(4)) comparator_1 (
    .a(AluIns), .b(4'b0011), .gt(comparator_1_gt), .eq(comparator_1_eq), .lt(comparator_1_lt));
  assign controlled_buffer_1_out = comparator_1_eq ? fpadder_1_out : 32'bz;  // Controlled_Buffer controlled_buffer_1
  assign controlled_buffer_1_out = comparator_1_lt ? fpmultiplier_1_out : 32'bz;  // Controlled_Buffer controlled_buffer_2
  assign controlled_buffer_1_out = comparator_1_gt ? fpsubtractor_1_out : 32'bz;  // Controlled_Buffer controlled_buffer_3
  assign AluOut = AluEn ? controlled_buffer_1_out : 32'bz;  // Controlled_Buffer controlled_buffer_4

  // Notes on the sheet:
  //   Add
  //   Multiply
  //   Subtract
endmodule

module InputStage (
  input  [31:0] InputIns,
  input  INP,
  input  CLK,
  output [3:0] InputStages
);

  wire not_1_out;
  wire [31:0] register_1_q;

  not not_1 (not_1_out, INP);
  Register #(.width(32)) register_1 (.D(InputIns), .en(not_1_out), .clk(CLK), .Q(register_1_q));  // open: clr
  // FPComparator fpcomparator_1: pin names not known; wires that end beside it: register_1_q, 32'h40000000, InputStages[0]
  // FPComparator fpcomparator_2: pin names not known; wires that end beside it: register_1_q, 32'h40000001, InputStages[1]
  // FPComparator fpcomparator_3: pin names not known; wires that end beside it: register_1_q, 32'h40000002, InputStages[2]
  // FPComparator fpcomparator_4: pin names not known; wires that end beside it: register_1_q, 32'h40000003, InputStages[3]
endmodule

module FOODS (
  input  WE,
  input  CLK,
  input  RST,
  input  in_4,
  input  in_5,
  input  in_6,
  output out_7,
  output out_8,
  output out_9,
  output [31:0] Stage_1_Output,
  output InputDone
);

  wire comparator_4_eq, comparator_5_eq, comparator_6_eq;
  wire [2:0] register_1_q;

  Register #(.width(3)) register_1 (.D({in_4, in_5, in_6}), .en(WE), .clk(CLK), .Q(register_1_q), .clr(RST));
  Comparator #(.width(3)) comparator_1 (.a(register_1_q), .b(3'b100), .eq(out_7));  // open: gt, lt
  Comparator #(.width(3)) comparator_2 (.a(register_1_q), .b(3'b010), .eq(out_8));  // open: gt, lt
  Comparator #(.width(3)) comparator_3 (.a(register_1_q), .b(3'b001), .eq(out_9));  // open: gt, lt
  Comparator #(.width(3)) comparator_4 (.a({in_4, in_5, in_6}), .b(3'b100), .eq(comparator_4_eq));  // open: gt, lt
  Comparator #(.width(3)) comparator_5 (.a({in_4, in_5, in_6}), .b(3'b010), .eq(comparator_5_eq));  // open: gt, lt
  Comparator #(.width(3)) comparator_6 (.a({in_4, in_5, in_6}), .b(3'b001), .eq(comparator_6_eq));  // open: gt, lt
  assign Stage_1_Output = comparator_4_eq ? 32'h424a0000 : 32'bz;  // Controlled_Buffer controlled_buffer_1
  assign Stage_1_Output = comparator_5_eq ? 32'h4270cccd : 32'bz;  // Controlled_Buffer controlled_buffer_2
  assign Stage_1_Output = comparator_6_eq ? 32'h42233333 : 32'bz;  // Controlled_Buffer controlled_buffer_3
  or or_1 (InputDone, comparator_4_eq, comparator_5_eq, comparator_6_eq);
endmodule

module QUANTITY (
  input  CLK,
  input  RST,
  input  inc,
  input  dec,
  output [7:0] AMOUNT,
  output [31:0] FloatAmount,
  output Done
);

  wire and_1_out, counter_1_carry, or_1_out;
  wire [31:0] controlled_buffer_1_out, fpadder_1_out, fpsubtractor_1_out;

  Counter #(.max('hd0)) counter_1 (.clk(CLK), .carry(counter_1_carry));  // open: clr, load, up, count, D, Q
  assign controlled_buffer_1_out = inc ? fpadder_1_out : 32'bz;  // Controlled_Buffer controlled_buffer_1
  assign controlled_buffer_1_out = and_1_out ? fpsubtractor_1_out : 32'bz;  // Controlled_Buffer controlled_buffer_2
  and and_1 (and_1_out, dec, Done);
  Register #(.width(32)) register_1 (
    .D(controlled_buffer_1_out), .en(or_1_out), .clk(counter_1_carry), .Q(FloatAmount), .clr(RST));
  or or_1 (or_1_out, inc, and_1_out);
  FPAdder fpadder_1 (.a(FloatAmount), .b(32'h3f800000), .out(fpadder_1_out));
  FPSubtractor fpsubtractor_1 (.a(FloatAmount), .b(32'h3f800000), .out(fpsubtractor_1_out));
  // FPComparator fpcomparator_1: pin names not known; wires that end beside it: FloatAmount, {32{1'b0}}, Done
  // FPToInt fptoint_1: pin names not known; wires that end beside it: FloatAmount, AMOUNT
endmodule

module Money (
  input  [31:0] enter_here,
  input  [31:0] total_charges,
  output out_3
);

  wire fpcomparator_1_p3, fpcomparator_1_p4;

  // FPComparator fpcomparator_1: pin names not known; wires that end beside it: enter_here, total_charges, fpcomparator_1_p3, fpcomparator_1_p4
  or or_1 (out_3, fpcomparator_1_p3, fpcomparator_1_p4);
endmodule

module OutputUnit (
  input  [1:0] OutputInst,
  output Out2,
  output Out1
);

  Comparator #(.mode("unsigned"), .width(2)) comparator_1 (
    .a(OutputInst), .b(2'b01), .gt(Out2), .eq(Out1));  // open: lt
endmodule
